# Fritzing sketch LineFollower (saved by Fritzing 1.0.2b)

parts:
  A1 = Adafruit v1.2 motor shield
  M1 = DC Motor [voltage_(max)=6V voltage_(min)=3V]
  VCC1 = Battery
  M2 = DC Motor [voltage_(max)=6V voltage_(min)=3V]
  U1 = SWITCH-SPST-2 [package=switch-spst-vertical]
  A2 = ky-033 [package=THT]
  A3 = ky-033 [package=THT]

nets:
  N1: A1.Pin_4, M2.pin_2
  N2: A1.Pin_5, M2.pin_1
  N3: A1.Pin_6, U1.O
  N4: A1.Pin_7, A1.Pin_12, A1.Pin_32, A1.Pin_33, A1.Pin_46, VCC1.-, A2.pin2, A2.pin3, A3.pin3
  N5: A1.Pin_26, A3.pin1
  N6: A1.Pin_27, A2.pin1
  N7: A1.Pin_38, A1.Pin_39, A2.pin4, A3.pin4
  N8: A1.Pin_47, M1.pin_2
  N9: A1.Pin_48, M1.pin_1
  N10: VCC1.+, U1.P

custom parts:
  Adafruit v1.2 motor shield: Adafruit v1.2 motor shield.
  ky-033: KY-033 Line successor module with TCRT5000 and analog output.
